// Logisim project 3Bits V 01.circ as structural Verilog: 13 circuits, main circuit halfadder
module halfadder (
  input  A,
  input  B,
  output S,
  output CO
);

  xor xor_1 (S, A, B);
  and and_1 (CO, A, B);
endmodule

module fulladder (
  input  CI,
  input  A,
  input  B,
  output S,
  output CO
);

  wire halfadder_1_co, halfadder_1_s, halfadder_2_co;

  halfadder halfadder_1 (.A(A), .B(B), .S(halfadder_1_s), .CO(halfadder_1_co));
  halfadder halfadder_2 (.A(CI), .B(halfadder_1_s), .S(S), .CO(halfadder_2_co));
  or or_1 (CO, halfadder_2_co, halfadder_1_co);
endmodule

module adder_3Bits (
  input  C0,
  input  A0,
  input  B0,
  input  A1,
  input  B1,
  input  A2,
  input  B2,
  output S0,
  output S1,
  output S2,
  output C3
);

  wire fulladder_1_co, fulladder_2_co;

  fulladder fulladder_1 (.CI(C0), .A(A0), .B(B0), .S(S0), .CO(fulladder_1_co));
  fulladder fulladder_2 (.CI(fulladder_1_co), .A(A1), .B(B1), .S(S1), .CO(fulladder_2_co));
  fulladder fulladder_3 (.CI(fulladder_2_co), .A(A2), .B(B2), .S(S2), .CO(C3));
endmodule

// A
module segment_a (
  input  In0,
  input  In1,
  input  In2,
  output A
);

  wire and_1_out, and_2_out, and_3_out, or_1_out;

  and and_1 (and_1_out, ~In0, In1);  // AND_Gate
  and and_2 (and_2_out, In0, ~In1);  // AND_Gate
  and and_3 (and_3_out, In0, In1, ~In2);  // AND_Gate
  or or_1 (or_1_out, and_1_out, and_2_out);
  or or_2 (A, or_1_out, and_3_out);
endmodule

// B
module segment_b (
  input  In0,
  input  In1,
  input  In2,
  output B
);

  wire and_1_out, and_2_out, and_3_out, or_1_out;

  and and_1 (and_1_out, In0, ~In1);  // AND_Gate
  and and_2 (and_2_out, ~In1, ~In2);  // AND_Gate
  and and_3 (and_3_out, In0, In1, ~In2);  // AND_Gate
  or or_1 (or_1_out, and_1_out, and_2_out);
  or or_2 (B, or_1_out, and_3_out);
endmodule

// C
module segment_c (
  input  In0,
  input  In1,
  input  In2,
  output C
);

  wire and_1_out, and_2_out, or_1_out;

  and and_1 (and_1_out, ~In0, ~In2, ~In1);  // AND_Gate
  and and_2 (and_2_out, In0, In2);
  or or_1 (or_1_out, and_1_out, and_2_out);
  or or_2 (C, In1, or_1_out);
endmodule

// D
module segment_d (
  input  In0,
  input  In1,
  input  In2,
  output D
);

  wire and_1_out, and_2_out, or_1_out;

  and and_1 (and_1_out, ~In2, ~In1);  // AND_Gate
  and and_2 (and_2_out, In1, In2);
  or or_1 (or_1_out, and_1_out, and_2_out);
  or or_2 (D, ~In0, or_1_out);  // OR_Gate
endmodule

// E
module segment_e (
  input  In0,
  input  In1,
  input  In2,
  output E
);

  wire and_1_out, and_2_out;

  and and_1 (and_1_out, In1, ~In2);  // AND_Gate
  and and_2 (and_2_out, ~In0, ~In2, ~In1);  // AND_Gate
  or or_1 (E, and_1_out, and_2_out);
endmodule

// F
module segment_f (
  input  In0,
  input  In1,
  input  In2,
  output F
);

  wire and_1_out, and_2_out, and_3_out, and_4_out, or_1_out, or_2_out;

  and and_1 (and_1_out, In0, In2, ~In1);  // AND_Gate
  and and_2 (and_2_out, ~In0, In2, In1);  // AND_Gate
  and and_3 (and_3_out, ~In0, ~In1, ~In2);  // AND_Gate
  and and_4 (and_4_out, In1, ~In2);  // AND_Gate
  or or_1 (or_1_out, and_1_out, and_2_out);
  or or_2 (or_2_out, and_3_out, and_4_out);
  or or_3 (F, or_1_out, or_2_out);
endmodule

// G
module segment_g (
  input  In0,
  input  In1,
  input  In2,
  output A
);

  wire and_1_out, and_2_out, or_1_out;

  and and_1 (and_1_out, In0, In1, ~In2);  // AND_Gate
  and and_2 (and_2_out, ~In1, ~In2);  // AND_Gate
  or or_1 (or_1_out, and_1_out, and_2_out);
  or or_2 (A, or_1_out, In2);
endmodule

module conversor_display (
  input  In0,
  input  In1,
  input  In2,
  output out_4,
  output out_5,
  output out_6,
  output out_7,
  output out_8,
  output out_9,
  output out_10
);

  segment_a segment_a_1 (.In0(In0), .In1(In1), .In2(In2), .A(out_4));
  segment_b segment_b_1 (.In0(In0), .In1(In1), .In2(In2), .B(out_5));
  segment_c segment_c_1 (.In0(In0), .In1(In1), .In2(In2), .C(out_6));
  segment_d segment_d_1 (.In0(In0), .In1(In1), .In2(In2), .D(out_7));
  segment_e segment_e_1 (.In0(In0), .In1(In1), .In2(In2), .E(out_8));
  segment_f segment_f_1 (.In0(In0), .In1(In1), .In2(In2), .F(out_9));
  segment_g segment_g_1 (.In0(In0), .In1(In1), .In2(In2), .A(out_10));
endmodule

module display (
  input  C1,
  input  A0,
  input  A1,
  input  A2,
  input  B0,
  input  B1,
  input  B2,
  output CO
);

  wire adder_3bits_1_s0, adder_3bits_1_s1, adder_3bits_1_s2, conversor_display_1_p4, conversor_display_1_p5,
       conversor_display_1_p6, conversor_display_1_p7, conversor_display_1_p8, conversor_display_1_p9,
       conversor_display_1_p10;

  adder_3Bits adder_3bits_1 (
    .C0(C1), .A0(A0), .B0(B0), .A1(A1), .B1(B1), .A2(A2), .B2(B2), .S0(adder_3bits_1_s0),
    .S1(adder_3bits_1_s1), .S2(adder_3bits_1_s2), .C3(CO));
  // conversor_display conversor_display_1: pin names not known; wires that end beside it: adder_3bits_1_s2, adder_3bits_1_s1, adder_3bits_1_s0, conversor_display_1_p4, conversor_display_1_p5, conversor_display_1_p6, conversor_display_1_p7, conversor_display_1_p8, conversor_display_1_p9, conversor_display_1_p10, conversor_display_1_p10, conversor_display_1_p10
  _7_Segment_Display u_7_segment_display_1 (
    .g(conversor_display_1_p4), .f(conversor_display_1_p5), .a(conversor_display_1_p9),
    .b(conversor_display_1_p6), .e(conversor_display_1_p10), .d(conversor_display_1_p7),
    .c(conversor_display_1_p8));  // open: dp
endmodule

module ProjetoFinal (
  input  in_1,
  input  in_2,
  input  in_3,
  input  in_4,
  input  in_5,
  input  in_6
);

  wire clock_1_out, conversor_display_1_out_4, conversor_display_1_out_5, conversor_display_1_out_6,
       conversor_display_1_out_7, conversor_display_1_out_8, conversor_display_1_out_9,
       conversor_display_1_out_10, main_1_out_7, main_1_out_8, main_1_out_9, registrador_1_out_5,
       registrador_1_out_6, registrador_1_out_7;

  _3Bits_V_01_main main_1 (
    .A(in_4), .B(in_1), .A_2(in_5), .B_2(in_2), .A_3(in_6), .B_3(in_3), .out_7(main_1_out_7),
    .out_8(main_1_out_8), .out_9(main_1_out_9));  // open: out_10
  Clock clock_1 (.out(clock_1_out));
  Registrador registrador_1 (
    .in_1(main_1_out_7), .in_2(main_1_out_8), .in_3(main_1_out_9), .S2(clock_1_out),
    .out_5(registrador_1_out_5), .out_6(registrador_1_out_6), .out_7(registrador_1_out_7));
  conversor_display conversor_display_1 (
    .In0(registrador_1_out_7), .In1(registrador_1_out_6), .In2(registrador_1_out_5),
    .out_4(conversor_display_1_out_4), .out_5(conversor_display_1_out_5), .out_6(conversor_display_1_out_6),
    .out_7(conversor_display_1_out_7), .out_8(conversor_display_1_out_8), .out_9(conversor_display_1_out_9),
    .out_10(conversor_display_1_out_10));
  _7_Segment_Display u_7_segment_display_1 (
    .g(conversor_display_1_out_4), .f(conversor_display_1_out_5), .a(conversor_display_1_out_6),
    .b(conversor_display_1_out_7), .e(conversor_display_1_out_8), .d(conversor_display_1_out_9),
    .c(conversor_display_1_out_10));  // open: dp
endmodule
