// Logisim project 3Bits V 02.circ as structural Verilog: 11 circuits, main circuit SomadorCompleto
// A
module segment_a (
  input  In0,
  input  In1,
  input  In2,
  output A
);

  wire and_1_out, and_2_out, and_3_out, or_1_out;

  and and_1 (and_1_out, ~In0, In1);  // AND_Gate
  and and_2 (and_2_out, In0, ~In1);  // AND_Gate
  and and_3 (and_3_out, In0, In1, ~In2);  // AND_Gate
  or or_1 (or_1_out, and_1_out, and_2_out);
  or or_2 (A, or_1_out, and_3_out);
endmodule

// B
module segment_b (
  input  In0,
  input  In1,
  input  In2,
  output B
);

  wire and_1_out, and_2_out, and_3_out, or_1_out;

  and and_1 (and_1_out, In0, ~In1);  // AND_Gate
  and and_2 (and_2_out, ~In1, ~In2);  // AND_Gate
  and and_3 (and_3_out, In0, In1, ~In2);  // AND_Gate
  or or_1 (or_1_out, and_1_out, and_2_out);
  or or_2 (B, or_1_out, and_3_out);
endmodule

// C
module segment_c (
  input  In0,
  input  In1,
  input  In2,
  output C
);

  wire and_1_out, and_2_out, or_1_out;

  and and_1 (and_1_out, ~In0, ~In2, ~In1);  // AND_Gate
  and and_2 (and_2_out, In0, In2);
  or or_1 (or_1_out, and_1_out, and_2_out);
  or or_2 (C, In1, or_1_out);
endmodule

// D
module segment_d (
  input  In0,
  input  In1,
  input  In2,
  output D
);

  wire and_1_out, and_2_out, or_1_out;

  and and_1 (and_1_out, ~In2, ~In1);  // AND_Gate
  and and_2 (and_2_out, In1, In2);
  or or_1 (or_1_out, and_1_out, and_2_out);
  or or_2 (D, ~In0, or_1_out);  // OR_Gate
endmodule

// E
module segment_e (
  input  In0,
  input  In1,
  input  In2,
  output E
);

  wire and_1_out, and_2_out;

  and and_1 (and_1_out, In1, ~In2);  // AND_Gate
  and and_2 (and_2_out, ~In0, ~In2, ~In1);  // AND_Gate
  or or_1 (E, and_1_out, and_2_out);
endmodule

// F
module segment_f (
  input  In0,
  input  In1,
  input  In2,
  output F
);

  wire and_1_out, and_2_out, and_3_out, and_4_out, or_1_out, or_2_out;

  and and_1 (and_1_out, In0, In2, ~In1);  // AND_Gate
  and and_2 (and_2_out, ~In0, In2, In1);  // AND_Gate
  and and_3 (and_3_out, ~In0, ~In1, ~In2);  // AND_Gate
  and and_4 (and_4_out, In1, ~In2);  // AND_Gate
  or or_1 (or_1_out, and_1_out, and_2_out);
  or or_2 (or_2_out, and_3_out, and_4_out);
  or or_3 (F, or_1_out, or_2_out);
endmodule

// G
module segment_g (
  input  In0,
  input  In1,
  input  In2,
  output A
);

  wire and_1_out, and_2_out, or_1_out;

  and and_1 (and_1_out, In0, In1, ~In2);  // AND_Gate
  and and_2 (and_2_out, ~In1, ~In2);  // AND_Gate
  or or_1 (or_1_out, and_1_out, and_2_out);
  or or_2 (A, or_1_out, In2);
endmodule

module conversor_display (
  input  In0,
  input  In1,
  input  In2,
  output out_4,
  output out_5,
  output out_6,
  output out_7,
  output out_8,
  output out_9,
  output out_10
);

  segment_a segment_a_1 (.In0(In0), .In1(In1), .In2(In2), .A(out_4));
  segment_b segment_b_1 (.In0(In0), .In1(In1), .In2(In2), .B(out_5));
  segment_c segment_c_1 (.In0(In0), .In1(In1), .In2(In2), .C(out_6));
  segment_d segment_d_1 (.In0(In0), .In1(In1), .In2(In2), .D(out_7));
  segment_e segment_e_1 (.In0(In0), .In1(In1), .In2(In2), .E(out_8));
  segment_f segment_f_1 (.In0(In0), .In1(In1), .In2(In2), .F(out_9));
  segment_g segment_g_1 (.In0(In0), .In1(In1), .In2(In2), .A(out_10));
endmodule

module FullAdder (
  input  A,
  input  B,
  input  A_2,
  input  B_2,
  input  A_3,
  input  B_3,
  output out_7,
  output out_8,
  output out_9,
  output out_10
);

  wire and_1_out, and_2_out, and_3_out, and_4_out, and_5_out, and_6_out, and_7_out, or_2_out, xor_1_out,
       xor_3_out;

  xor xor_1 (xor_1_out, A, B);
  and and_1 (and_1_out, A, or_2_out);
  and and_2 (and_2_out, B, A);
  and and_3 (and_3_out, or_2_out, B);
  xor xor_2 (out_7, xor_1_out, or_2_out);
  or or_1 (out_10, and_1_out, and_2_out, and_3_out);
  xor xor_3 (xor_3_out, A_2, B_2);
  and and_4 (and_4_out, A_2, and_7_out);
  and and_5 (and_5_out, B_2, A_2);
  and and_6 (and_6_out, and_7_out, B_2);
  xor xor_4 (out_8, xor_3_out, and_7_out);
  or or_2 (or_2_out, and_4_out, and_5_out, and_6_out);
  xor xor_5 (out_9, B_3, A_3);
  and and_7 (and_7_out, A_3, B_3);
endmodule

module Registrador (
  input  in_1,
  input  in_2,
  input  in_3,
  input  S2,
  output out_5,
  output out_6,
  output out_7
);

  D_Flip_Flop d_ff_1 (.clk(S2), .D(in_3), .Q(out_5));  // open: Qn, preset, en, reset
  D_Flip_Flop d_ff_2 (.clk(S2), .D(in_2), .Q(out_6));  // open: Qn, preset, en, reset
  D_Flip_Flop d_ff_3 (.clk(S2), .D(in_1), .Q(out_7));  // open: Qn, preset, en, reset
endmodule

module SomadorCompleto (
  input  in_1,
  input  in_2,
  input  in_3,
  input  in_4,
  input  in_5,
  input  in_6
);

  wire clock_1_out, conversor_display_1_out_4, conversor_display_1_out_5, conversor_display_1_out_6,
       conversor_display_1_out_7, conversor_display_1_out_8, conversor_display_1_out_9,
       conversor_display_1_out_10, fulladder_1_out_7, fulladder_1_out_8, fulladder_1_out_9,
       registrador_1_out_5, registrador_1_out_6, registrador_1_out_7;

  FullAdder fulladder_1 (
    .out_7(fulladder_1_out_7), .out_8(fulladder_1_out_8), .out_9(fulladder_1_out_9), .A(in_4), .B(in_1),
    .A_2(in_5), .B_2(in_2), .A_3(in_6), .B_3(in_3));  // open: out_10
  Registrador registrador_1 (
    .in_1(fulladder_1_out_7), .in_2(fulladder_1_out_8), .in_3(fulladder_1_out_9), .S2(clock_1_out),
    .out_5(registrador_1_out_5), .out_6(registrador_1_out_6), .out_7(registrador_1_out_7));
  Clock clock_1 (.out(clock_1_out));
  conversor_display conversor_display_1 (
    .In0(registrador_1_out_7), .In1(registrador_1_out_6), .In2(registrador_1_out_5),
    .out_4(conversor_display_1_out_4), .out_5(conversor_display_1_out_5), .out_6(conversor_display_1_out_6),
    .out_7(conversor_display_1_out_7), .out_8(conversor_display_1_out_8), .out_9(conversor_display_1_out_9),
    .out_10(conversor_display_1_out_10));
  _7_Segment_Display u_7_segment_display_1 (
    .g(conversor_display_1_out_4), .f(conversor_display_1_out_5), .a(conversor_display_1_out_6),
    .b(conversor_display_1_out_7), .e(conversor_display_1_out_8), .d(conversor_display_1_out_9),
    .c(conversor_display_1_out_10));  // open: dp
endmodule
